// Logisim project synchronous_model.circ as structural Verilog: 10 circuits, main circuit main
module main (
  input  in_1,
  input  in_2,
  input  in_3,
  input  in_4,
  input  in_5,
  input  in_6,
  input  in_7,
  input  in_8,
  input  in_9,
  input  in_10
);

  wire bcd_to_seven_1_a, bcd_to_seven_1_b, bcd_to_seven_1_c, bcd_to_seven_1_d, bcd_to_seven_1_e,
       bcd_to_seven_1_f, bcd_to_seven_1_g, bcd_to_seven_2_a, bcd_to_seven_2_b, bcd_to_seven_2_c,
       bcd_to_seven_2_d, bcd_to_seven_2_e, bcd_to_seven_2_f, bcd_to_seven_2_g, bcd_to_seven_3_a,
       bcd_to_seven_3_b, bcd_to_seven_3_c, bcd_to_seven_3_d, bcd_to_seven_3_e, bcd_to_seven_3_f,
       bcd_to_seven_3_g, bcd_to_seven_4_a, bcd_to_seven_4_b, bcd_to_seven_4_c, bcd_to_seven_4_d,
       bcd_to_seven_4_e, bcd_to_seven_4_f, bcd_to_seven_4_g, bcd_to_seven_5_a, bcd_to_seven_5_b,
       bcd_to_seven_5_c, bcd_to_seven_5_d, bcd_to_seven_5_e, bcd_to_seven_5_f, bcd_to_seven_5_g,
       bcd_to_seven_6_a, bcd_to_seven_6_b, bcd_to_seven_6_c, bcd_to_seven_6_d, bcd_to_seven_6_e,
       bcd_to_seven_6_f, bcd_to_seven_6_g, bcd_to_seven_7_a, bcd_to_seven_7_b, bcd_to_seven_7_c,
       bcd_to_seven_7_d, bcd_to_seven_7_e, bcd_to_seven_7_f, bcd_to_seven_7_g, bcd_to_seven_8_a,
       bcd_to_seven_8_b, bcd_to_seven_8_c, bcd_to_seven_8_d, bcd_to_seven_8_e, bcd_to_seven_8_f,
       bcd_to_seven_8_g, button_1_out, button_2_out, button_3_out, display_7_segment_1_out_11,
       display_7_segment_1_out_12, display_7_segment_1_out_13, display_7_segment_1_out_14,
       display_7_segment_1_out_15, display_7_segment_1_out_16, display_7_segment_1_out_17,
       display_7_segment_1_out_18, display_7_segment_1_out_19, display_7_segment_1_out_20,
       display_7_segment_1_out_21, display_7_segment_1_out_22, display_7_segment_1_out_23,
       display_7_segment_1_out_24, display_7_segment_1_out_25, display_7_segment_1_out_26,
       display_7_segment_2_out_11, display_7_segment_2_out_12, display_7_segment_2_out_13,
       display_7_segment_2_out_14, display_7_segment_2_out_15, display_7_segment_2_out_16,
       display_7_segment_2_out_17, display_7_segment_2_out_18, display_7_segment_2_out_19,
       display_7_segment_2_out_20, display_7_segment_2_out_21, display_7_segment_2_out_22,
       display_7_segment_2_out_23, display_7_segment_2_out_24, display_7_segment_2_out_25,
       display_7_segment_2_out_26, modified_counter_1_lsb, modified_counter_1_msb, modified_counter_1_out_15,
       modified_counter_1_out_16, modified_counter_1_out_17, modified_counter_1_out_18,
       modified_counter_1_out_19, modified_counter_1_out_20, modified_counter_1_out_21,
       modified_counter_1_out_22, modified_counter_1_out_24, modified_counter_1_out_25;

  Button button_1 (.out(button_1_out));
  LED led_1 (.in(modified_counter_1_out_24));
  LED led_2 (.in(modified_counter_1_out_24));
  LED led_3 (.in(modified_counter_1_out_24));
  LED led_4 (.in(modified_counter_1_out_25));
  Button button_2 (.out(button_2_out));
  _7_Segment_Display u_7_segment_display_1 (
    .g(bcd_to_seven_1_g), .f(bcd_to_seven_1_f), .a(bcd_to_seven_1_a), .b(bcd_to_seven_1_b),
    .e(bcd_to_seven_1_e), .d(bcd_to_seven_1_d), .c(bcd_to_seven_1_c));  // open: dp
  BCD_to_seven bcd_to_seven_1 (
    .A3(display_7_segment_1_out_11), .A2(display_7_segment_1_out_12), .A1(display_7_segment_1_out_13),
    .A0(display_7_segment_1_out_14), .a(bcd_to_seven_1_a), .b(bcd_to_seven_1_b), .c(bcd_to_seven_1_c),
    .d(bcd_to_seven_1_d), .e(bcd_to_seven_1_e), .f(bcd_to_seven_1_f), .g(bcd_to_seven_1_g));
  Display_7_segment display_7_segment_1 (
    .in_1(modified_counter_1_msb), .in_2(modified_counter_1_out_15), .in_3(modified_counter_1_out_16),
    .in_4(modified_counter_1_out_17), .in_5(modified_counter_1_out_18), .in_6(modified_counter_1_out_19),
    .in_7(modified_counter_1_out_20), .in_8(modified_counter_1_out_21), .in_9(modified_counter_1_out_22),
    .in_10(modified_counter_1_lsb), .out_11(display_7_segment_1_out_11), .out_12(display_7_segment_1_out_12),
    .out_13(display_7_segment_1_out_13), .out_14(display_7_segment_1_out_14),
    .out_15(display_7_segment_1_out_15), .out_16(display_7_segment_1_out_16),
    .out_17(display_7_segment_1_out_17), .out_18(display_7_segment_1_out_18),
    .out_19(display_7_segment_1_out_19), .out_20(display_7_segment_1_out_20),
    .out_21(display_7_segment_1_out_21), .out_22(display_7_segment_1_out_22),
    .out_23(display_7_segment_1_out_23), .out_24(display_7_segment_1_out_24),
    .out_25(display_7_segment_1_out_25), .out_26(display_7_segment_1_out_26));
  _7_Segment_Display u_7_segment_display_2 (
    .g(bcd_to_seven_2_g), .f(bcd_to_seven_2_f), .a(bcd_to_seven_2_a), .b(bcd_to_seven_2_b),
    .e(bcd_to_seven_2_e), .d(bcd_to_seven_2_d), .c(bcd_to_seven_2_c));  // open: dp
  modified_counter modified_counter_1 (
    .Up_count(button_2_out), .Down_count(button_1_out), .in_1(in_1), .in_2(in_2), .in_3(in_3), .in_4(in_4),
    .in_5(in_5), .in_6(in_6), .in_7(in_7), .in_8(in_8), .in_9(in_9), .in_10(in_10),
    .out_25(modified_counter_1_out_25), .MSB(modified_counter_1_msb), .out_15(modified_counter_1_out_15),
    .out_16(modified_counter_1_out_16), .out_17(modified_counter_1_out_17),
    .out_18(modified_counter_1_out_18), .out_19(modified_counter_1_out_19),
    .out_20(modified_counter_1_out_20), .out_21(modified_counter_1_out_21),
    .out_22(modified_counter_1_out_22), .LSB(modified_counter_1_lsb), .out_24(modified_counter_1_out_24),
    .Reset(button_3_out));
  BCD_to_seven bcd_to_seven_2 (
    .A3(display_7_segment_1_out_15), .A2(display_7_segment_1_out_16), .A1(display_7_segment_1_out_17),
    .A0(display_7_segment_1_out_18), .a(bcd_to_seven_2_a), .b(bcd_to_seven_2_b), .c(bcd_to_seven_2_c),
    .d(bcd_to_seven_2_d), .e(bcd_to_seven_2_e), .f(bcd_to_seven_2_f), .g(bcd_to_seven_2_g));
  Button button_3 (.out(button_3_out));
  BCD_to_seven bcd_to_seven_3 (
    .A3(display_7_segment_1_out_19), .A2(display_7_segment_1_out_20), .A1(display_7_segment_1_out_21),
    .A0(display_7_segment_1_out_22), .a(bcd_to_seven_3_a), .b(bcd_to_seven_3_b), .c(bcd_to_seven_3_c),
    .d(bcd_to_seven_3_d), .e(bcd_to_seven_3_e), .f(bcd_to_seven_3_f), .g(bcd_to_seven_3_g));
  _7_Segment_Display u_7_segment_display_3 (
    .g(bcd_to_seven_3_g), .f(bcd_to_seven_3_f), .a(bcd_to_seven_3_a), .b(bcd_to_seven_3_b),
    .e(bcd_to_seven_3_e), .d(bcd_to_seven_3_d), .c(bcd_to_seven_3_c));  // open: dp
  _7_Segment_Display u_7_segment_display_4 (
    .g(bcd_to_seven_4_g), .f(bcd_to_seven_4_f), .a(bcd_to_seven_4_a), .b(bcd_to_seven_4_b),
    .e(bcd_to_seven_4_e), .d(bcd_to_seven_4_d), .c(bcd_to_seven_4_c));  // open: dp
  BCD_to_seven bcd_to_seven_4 (
    .A3(display_7_segment_1_out_23), .A2(display_7_segment_1_out_24), .A1(display_7_segment_1_out_25),
    .A0(display_7_segment_1_out_26), .a(bcd_to_seven_4_a), .b(bcd_to_seven_4_b), .c(bcd_to_seven_4_c),
    .d(bcd_to_seven_4_d), .e(bcd_to_seven_4_e), .f(bcd_to_seven_4_f), .g(bcd_to_seven_4_g));
  BCD_to_seven bcd_to_seven_5 (
    .A3(display_7_segment_2_out_11), .A2(display_7_segment_2_out_12), .A1(display_7_segment_2_out_13),
    .A0(display_7_segment_2_out_14), .a(bcd_to_seven_5_a), .b(bcd_to_seven_5_b), .c(bcd_to_seven_5_c),
    .d(bcd_to_seven_5_d), .e(bcd_to_seven_5_e), .f(bcd_to_seven_5_f), .g(bcd_to_seven_5_g));
  _7_Segment_Display u_7_segment_display_5 (
    .g(bcd_to_seven_5_g), .f(bcd_to_seven_5_f), .a(bcd_to_seven_5_a), .b(bcd_to_seven_5_b),
    .e(bcd_to_seven_5_e), .d(bcd_to_seven_5_d), .c(bcd_to_seven_5_c));  // open: dp
  Display_7_segment display_7_segment_2 (
    .in_1(in_1), .in_2(in_2), .in_3(in_3), .in_4(in_4), .in_5(in_5), .in_6(in_6), .in_7(in_7), .in_8(in_8),
    .in_9(in_9), .in_10(in_10), .out_11(display_7_segment_2_out_11), .out_12(display_7_segment_2_out_12),
    .out_13(display_7_segment_2_out_13), .out_14(display_7_segment_2_out_14),
    .out_15(display_7_segment_2_out_15), .out_16(display_7_segment_2_out_16),
    .out_17(display_7_segment_2_out_17), .out_18(display_7_segment_2_out_18),
    .out_19(display_7_segment_2_out_19), .out_20(display_7_segment_2_out_20),
    .out_21(display_7_segment_2_out_21), .out_22(display_7_segment_2_out_22),
    .out_23(display_7_segment_2_out_23), .out_24(display_7_segment_2_out_24),
    .out_25(display_7_segment_2_out_25), .out_26(display_7_segment_2_out_26));
  BCD_to_seven bcd_to_seven_6 (
    .A3(display_7_segment_2_out_15), .A2(display_7_segment_2_out_16), .A1(display_7_segment_2_out_17),
    .A0(display_7_segment_2_out_18), .a(bcd_to_seven_6_a), .b(bcd_to_seven_6_b), .c(bcd_to_seven_6_c),
    .d(bcd_to_seven_6_d), .e(bcd_to_seven_6_e), .f(bcd_to_seven_6_f), .g(bcd_to_seven_6_g));
  _7_Segment_Display u_7_segment_display_6 (
    .g(bcd_to_seven_6_g), .f(bcd_to_seven_6_f), .a(bcd_to_seven_6_a), .b(bcd_to_seven_6_b),
    .e(bcd_to_seven_6_e), .d(bcd_to_seven_6_d), .c(bcd_to_seven_6_c));  // open: dp
  BCD_to_seven bcd_to_seven_7 (
    .A3(display_7_segment_2_out_19), .A2(display_7_segment_2_out_20), .A1(display_7_segment_2_out_21),
    .A0(display_7_segment_2_out_22), .a(bcd_to_seven_7_a), .b(bcd_to_seven_7_b), .c(bcd_to_seven_7_c),
    .d(bcd_to_seven_7_d), .e(bcd_to_seven_7_e), .f(bcd_to_seven_7_f), .g(bcd_to_seven_7_g));
  _7_Segment_Display u_7_segment_display_7 (
    .g(bcd_to_seven_7_g), .f(bcd_to_seven_7_f), .a(bcd_to_seven_7_a), .b(bcd_to_seven_7_b),
    .e(bcd_to_seven_7_e), .d(bcd_to_seven_7_d), .c(bcd_to_seven_7_c));  // open: dp
  BCD_to_seven bcd_to_seven_8 (
    .A3(display_7_segment_2_out_23), .A2(display_7_segment_2_out_24), .A1(display_7_segment_2_out_25),
    .A0(display_7_segment_2_out_26), .a(bcd_to_seven_8_a), .b(bcd_to_seven_8_b), .c(bcd_to_seven_8_c),
    .d(bcd_to_seven_8_d), .e(bcd_to_seven_8_e), .f(bcd_to_seven_8_f), .g(bcd_to_seven_8_g));
  _7_Segment_Display u_7_segment_display_8 (
    .g(bcd_to_seven_8_g), .f(bcd_to_seven_8_f), .a(bcd_to_seven_8_a), .b(bcd_to_seven_8_b),
    .e(bcd_to_seven_8_e), .d(bcd_to_seven_8_d), .c(bcd_to_seven_8_c));  // open: dp

  // Notes on the sheet:
  //   EXIT
  //   (Press when person exits)
  //   Exit door
  //   LED (POWER)
  //   *** ROOM ***
  //   Entry door
  //   LED (POWER)
  //   ENTRY
  //   (Press when person enters)
  //   AUTOMATIC ROOM POWER CONTROLLER WITH BIDIRECTIONAL VISITOR COUNTER
  //   Input maximum limit
  //   Reset
  //   COUNT
  //   MAX LIMIT
endmodule

module Mux (
  input  Input_1,
  input  Input_2,
  input  Select_bit,
  output out_4
);

  wire and_1_out, and_2_out, not_1_out;

  not not_1 (not_1_out, Select_bit);
  and and_1 (and_1_out, not_1_out, Input_1);
  and and_2 (and_2_out, Select_bit, Input_2);
  or or_1 (out_4, and_1_out, and_2_out);

  // Notes on the sheet:
  //   2 to 1 Multiplexer
endmodule

module SR_Latch (
  input  S,
  input  R,
  output Q,
  output Q_prime
);

  nor nor_1 (Q, R, Q_prime);
  nor nor_2 (Q_prime, Q, S);

  // Notes on the sheet:
  //   SR Latch
endmodule

module synchronous_counter (
  input  Toggle,
  input  Up_count,
  input  Down_count,
  input  Reset,
  output MSB,
  output out_6,
  output out_7,
  output out_8,
  output out_9,
  output out_10,
  output out_11,
  output out_12,
  output out_13,
  output LSB
);

  wire and_1_out, and_2_out, and_3_out, and_4_out, and_5_out, and_6_out, and_7_out, and_8_out, and_9_out,
       and_10_out, and_11_out, and_12_out, and_13_out, and_14_out, and_15_out, and_16_out, and_17_out,
       and_18_out, j_k_ff_1_qn, j_k_ff_2_qn, j_k_ff_3_qn, j_k_ff_4_qn, j_k_ff_5_qn, j_k_ff_6_qn, j_k_ff_7_qn,
       j_k_ff_8_qn, j_k_ff_9_qn, not_1_out, not_2_out, or_1_out, or_2_out, or_3_out, or_4_out, or_5_out,
       or_6_out, or_7_out, or_8_out, or_9_out, or_10_out, sr_latch_1_q;

  SR_Latch sr_latch_1 (.S(Up_count), .R(Down_count), .Q(sr_latch_1_q));  // open: Q_prime
  or or_1 (or_1_out, Down_count, Up_count);
  not not_1 (not_1_out, or_1_out);
  J_K_Flip_Flop j_k_ff_1 (
    .J(Toggle), .clk(not_1_out), .K(Toggle), .Q(LSB), .Qn(j_k_ff_1_qn), .reset(Reset));  // open: preset, en
  not not_2 (not_2_out, sr_latch_1_q);
  and and_1 (and_1_out, sr_latch_1_q, LSB);
  and and_2 (and_2_out, j_k_ff_1_qn, not_2_out);
  or or_2 (or_2_out, and_1_out, and_2_out);
  J_K_Flip_Flop j_k_ff_2 (
    .J(or_2_out), .clk(not_1_out), .K(or_2_out), .Q(out_13), .Qn(j_k_ff_2_qn), .reset(Reset));  // open: preset, en
  and and_3 (and_3_out, and_1_out, out_13);
  and and_4 (and_4_out, j_k_ff_2_qn, and_2_out);
  or or_3 (or_3_out, and_3_out, and_4_out);
  and and_5 (and_5_out, and_3_out, out_12);
  J_K_Flip_Flop j_k_ff_3 (
    .J(or_3_out), .clk(not_1_out), .K(or_3_out), .Q(out_12), .Qn(j_k_ff_3_qn), .reset(Reset));  // open: preset, en
  and and_6 (and_6_out, j_k_ff_3_qn, and_4_out);
  or or_4 (or_4_out, and_5_out, and_6_out);
  J_K_Flip_Flop j_k_ff_4 (
    .J(or_4_out), .clk(not_1_out), .K(or_4_out), .Q(out_11), .Qn(j_k_ff_4_qn), .reset(Reset));  // open: preset, en
  and and_7 (and_7_out, and_5_out, out_11);
  and and_8 (and_8_out, j_k_ff_4_qn, and_6_out);
  or or_5 (or_5_out, and_7_out, and_8_out);
  J_K_Flip_Flop j_k_ff_5 (
    .J(or_5_out), .clk(not_1_out), .K(or_5_out), .Q(out_10), .Qn(j_k_ff_5_qn), .reset(Reset));  // open: preset, en
  and and_9 (and_9_out, and_7_out, out_10);
  and and_10 (and_10_out, j_k_ff_5_qn, and_8_out);
  or or_6 (or_6_out, and_9_out, and_10_out);
  J_K_Flip_Flop j_k_ff_6 (
    .J(or_6_out), .clk(not_1_out), .K(or_6_out), .Q(out_9), .Qn(j_k_ff_6_qn), .reset(Reset));  // open: preset, en
  and and_11 (and_11_out, and_9_out, out_9);
  and and_12 (and_12_out, j_k_ff_6_qn, and_10_out);
  or or_7 (or_7_out, and_11_out, and_12_out);
  J_K_Flip_Flop j_k_ff_7 (
    .J(or_7_out), .clk(not_1_out), .K(or_7_out), .Q(out_8), .Qn(j_k_ff_7_qn), .reset(Reset));  // open: preset, en
  and and_13 (and_13_out, and_11_out, out_8);
  and and_14 (and_14_out, j_k_ff_7_qn, and_12_out);
  or or_8 (or_8_out, and_13_out, and_14_out);
  J_K_Flip_Flop j_k_ff_8 (
    .J(or_8_out), .clk(not_1_out), .K(or_8_out), .Q(out_7), .Qn(j_k_ff_8_qn), .reset(Reset));  // open: preset, en
  and and_15 (and_15_out, and_13_out, out_7);
  and and_16 (and_16_out, j_k_ff_8_qn, and_14_out);
  or or_9 (or_9_out, and_15_out, and_16_out);
  J_K_Flip_Flop j_k_ff_9 (
    .J(or_9_out), .clk(not_1_out), .K(or_9_out), .Q(out_6), .Qn(j_k_ff_9_qn), .reset(Reset));  // open: preset, en
  and and_17 (and_17_out, and_15_out, out_6);
  and and_18 (and_18_out, j_k_ff_9_qn, and_16_out);
  or or_10 (or_10_out, and_17_out, and_18_out);
  J_K_Flip_Flop j_k_ff_10 (
    .J(or_10_out), .clk(not_1_out), .K(or_10_out), .Q(MSB), .reset(Reset));  // open: Qn, preset, en

  // Notes on the sheet:
  //   SR Latch
  //   Clock
  //   10 bit synchronous up/down counter 
  //   COUNT
endmodule

module modified_counter (
  input  in_1,
  input  in_2,
  input  in_3,
  input  in_4,
  input  in_5,
  input  in_6,
  input  in_7,
  input  in_8,
  input  in_9,
  input  in_10,
  input  Up_count,
  input  Reset,
  input  Down_count,
  output MSB,
  output out_15,
  output out_16,
  output out_17,
  output out_18,
  output out_19,
  output out_20,
  output out_21,
  output out_22,
  output LSB,
  output out_24,
  output out_25
);

  wire and_1_out, Mux_2_out_4, mux_3_out_4, mux_4_out_4, mux_5_out_4, mux_6_out_4, mux_7_out_4, mux_8_out_4,
       mux_9_out_4, mux_10_out_4, mux_11_out_4, mux_12_out_4, Mux_out_4, nor_1_out, not_2_out, not_3_out,
       not_5_out, not_6_out, not_7_out, not_8_out, not_9_out, not_10_out, not_11_out, not_12_out, not_13_out,
       not_14_out;

  not not_1 (out_25, and_1_out);
  Mux Mux (.Input_1(Down_count), .Input_2(not_2_out), .Select_bit(nor_1_out), .out_4(Mux_out_4));
  not not_2 (not_2_out, 1'b1);
  not not_3 (not_3_out, 1'b1);
  not not_4 (out_24, nor_1_out);
  Mux Mux_2 (.Input_1(Up_count), .Input_2(not_3_out), .Select_bit(and_1_out), .out_4(Mux_2_out_4));
  nor nor_1 (nor_1_out, MSB, out_15, out_16, out_17, out_18, out_19, out_20, out_21, out_22, LSB);
  synchronous_counter synchronous_counter_1 (
    .Up_count(Mux_2_out_4), .Down_count(Mux_out_4), .Toggle(1'b1), .MSB(MSB), .out_6(out_15), .out_7(out_16),
    .out_8(out_17), .out_9(out_18), .out_10(out_19), .out_11(out_20), .out_12(out_21), .out_13(out_22),
    .LSB(LSB), .Reset(Reset));
  not not_5 (not_5_out, out_15);
  not not_6 (not_6_out, MSB);
  Mux mux_3 (.Input_1(not_5_out), .Input_2(out_15), .Select_bit(in_2), .out_4(mux_3_out_4));
  Mux mux_4 (.Input_1(not_6_out), .Input_2(MSB), .Select_bit(in_1), .out_4(mux_4_out_4));
  not not_7 (not_7_out, out_16);
  Mux mux_5 (.Input_1(not_7_out), .Input_2(out_16), .Select_bit(in_3), .out_4(mux_5_out_4));
  not not_8 (not_8_out, out_17);
  not not_9 (not_9_out, out_18);
  Mux mux_6 (.Input_1(not_8_out), .Input_2(out_17), .Select_bit(in_4), .out_4(mux_6_out_4));
  Mux mux_7 (.Input_1(not_9_out), .Input_2(out_18), .Select_bit(in_5), .out_4(mux_7_out_4));
  not not_10 (not_10_out, out_20);
  not not_11 (not_11_out, out_19);
  Mux mux_8 (.Input_1(not_11_out), .Input_2(out_19), .Select_bit(in_6), .out_4(mux_8_out_4));
  Mux mux_9 (.Input_1(not_10_out), .Input_2(out_20), .Select_bit(in_7), .out_4(mux_9_out_4));
  and and_1 (and_1_out, mux_4_out_4, mux_3_out_4, mux_5_out_4, mux_6_out_4, mux_7_out_4, mux_8_out_4, mux_9_out_4, mux_10_out_4, mux_12_out_4, mux_11_out_4);
  not not_12 (not_12_out, out_21);
  Mux mux_10 (.Input_1(not_12_out), .Input_2(out_21), .Select_bit(in_8), .out_4(mux_10_out_4));
  not not_13 (not_13_out, LSB);
  not not_14 (not_14_out, out_22);
  Mux mux_11 (.Input_1(not_13_out), .Input_2(LSB), .Select_bit(in_10), .out_4(mux_11_out_4));
  Mux mux_12 (.Input_1(not_14_out), .Input_2(out_22), .Select_bit(in_9), .out_4(mux_12_out_4));

  // Notes on the sheet:
  //   Entry door control
  //   Visitor counter
  //   Check underflow
  //   Toggle
  //   COUNT
  //   Check light on/off
  //   Check overflow
endmodule

module check3 (
  input  in_1,
  input  in_2,
  input  in_3,
  input  in_4,
  output out_5,
  output out_6,
  output out_7,
  output out_8,
  output out_9
);

  wire and_1_out, not_1_out, not_2_out, not_3_out, or_1_out, or_2_out;

  not not_1 (not_1_out, 1'b1);
  _4_bit_full_adder u_4_bit_full_adder_1 (
    .Cin(not_1_out), .in_6(in_1), .A(in_2), .in_8(in_3), .in_9(in_4), .in_1(not_2_out), .B(not_3_out),
    .in_3(or_1_out), .in_4(or_1_out), .Cout(out_5), .out_11(out_6), .Sum(out_7), .out_13(out_8),
    .out_14(out_9));
  not not_2 (not_2_out, 1'b1);
  not not_3 (not_3_out, 1'b1);
  or or_1 (or_1_out, in_1, and_1_out);
  or or_2 (or_2_out, in_3, in_4);
  and and_1 (and_1_out, in_2, or_2_out);
endmodule

module _1_bit_full_adder (
  input  A,
  input  B,
  input  Cin,
  output Sum,
  output Carry
);

  wire and_1_out, and_2_out, xor_1_out;

  xor xor_1 (xor_1_out, A, B);
  xor xor_2 (Sum, xor_1_out, Cin);
  and and_1 (and_1_out, xor_1_out, Cin);
  and and_2 (and_2_out, A, B);
  or or_1 (Carry, and_1_out, and_2_out);
endmodule

module _4_bit_full_adder (
  input  in_1,
  input  B,
  input  in_3,
  input  in_4,
  input  Cin,
  input  in_6,
  input  A,
  input  in_8,
  input  in_9,
  output Cout,
  output out_11,
  output Sum,
  output out_13,
  output out_14
);

  wire n1_bit_full_adder_1_carry, n1_bit_full_adder_2_carry, n1_bit_full_adder_3_carry;

  _1_bit_full_adder u_1_bit_full_adder_1 (
    .A(in_9), .B(in_4), .Cin(Cin), .Sum(out_14), .Carry(n1_bit_full_adder_1_carry));
  _1_bit_full_adder u_1_bit_full_adder_2 (
    .A(in_8), .B(in_3), .Cin(n1_bit_full_adder_1_carry), .Sum(out_13), .Carry(n1_bit_full_adder_2_carry));
  _1_bit_full_adder u_1_bit_full_adder_3 (
    .A(A), .B(B), .Cin(n1_bit_full_adder_2_carry), .Sum(Sum), .Carry(n1_bit_full_adder_3_carry));
  _1_bit_full_adder u_1_bit_full_adder_4 (
    .A(in_6), .B(in_1), .Cin(n1_bit_full_adder_3_carry), .Sum(out_11), .Carry(Cout));
endmodule

module BCD_to_seven (
  input  A3,
  input  A2,
  input  A1,
  input  A0,
  output a,
  output b,
  output c,
  output d,
  output e,
  output f,
  output g
);

  wire and_1_out, and_2_out, and_3_out, and_4_out, and_5_out, and_6_out, and_7_out, and_8_out, and_9_out,
       not_1_out, not_2_out, not_3_out, not_4_out;

  not not_1 (not_1_out, A3);
  not not_2 (not_2_out, A2);
  not not_3 (not_3_out, A1);
  not not_4 (not_4_out, A0);
  and and_1 (and_1_out, A2, A0);
  and and_2 (and_2_out, not_2_out, not_4_out);
  and and_3 (and_3_out, A1, A0);
  and and_4 (and_4_out, not_3_out, not_4_out);
  or or_1 (c, A2, not_3_out, A0);
  and and_5 (and_5_out, A1, not_4_out);
  and and_6 (and_6_out, not_2_out, A1);
  and and_7 (and_7_out, A2, not_3_out);
  and and_8 (and_8_out, A2, not_4_out);
  and and_9 (and_9_out, A0, and_7_out);
  or or_2 (a, and_1_out, and_2_out, A3, A1);
  or or_3 (d, A3, and_2_out, and_5_out, and_6_out, and_9_out);
  or or_4 (b, and_3_out, and_4_out, not_2_out);
  or or_5 (e, and_2_out, and_5_out);
  or or_6 (f, and_4_out, and_7_out, A3, and_8_out);
  or or_7 (g, and_5_out, and_6_out, A3, and_7_out);
endmodule

module Display_7_segment (
  input  in_1,
  input  in_2,
  input  in_3,
  input  in_4,
  input  in_5,
  input  in_6,
  input  in_7,
  input  in_8,
  input  in_9,
  input  in_10,
  output out_11,
  output out_12,
  output out_13,
  output out_14,
  output out_15,
  output out_16,
  output out_17,
  output out_18,
  output out_19,
  output out_20,
  output out_21,
  output out_22,
  output out_23,
  output out_24,
  output out_25,
  output out_26
);

  wire check3_1_out_7, check3_1_out_8, check3_1_out_9, check3_2_out_7, check3_2_out_8, check3_2_out_9,
       check3_3_out_7, check3_3_out_8, check3_3_out_9, check3_5_out_7, check3_5_out_8, check3_5_out_9,
       check3_6_out_7, check3_6_out_8, check3_6_out_9, check3_7_out_7, check3_7_out_8, check3_7_out_9,
       check3_8_out_6, check3_8_out_7, check3_8_out_8, check3_8_out_9, check3_9_out_6, check3_9_out_7,
       check3_9_out_8, check3_9_out_9, check3_10_out_6, check3_10_out_7, check3_10_out_8, check3_10_out_9,
       check3_11_out_6, check3_11_out_7, check3_11_out_8, check3_11_out_9, check3_13_out_6, check3_13_out_7,
       check3_13_out_8, check3_13_out_9, check3_14_out_6, check3_14_out_7, check3_14_out_8, check3_14_out_9,
       check3_15_out_6, check3_15_out_7, check3_15_out_8, check3_15_out_9, check3_16_out_6, check3_16_out_7,
       check3_16_out_8, check3_16_out_9, check3_17_out_6, check3_17_out_7, check3_17_out_8, check3_17_out_9,
       check3_18_out_6, check3_18_out_7, check3_18_out_8, check3_18_out_9, check3_19_out_6, check3_19_out_7,
       check3_19_out_8, check3_19_out_9, check3_20_out_6, check3_20_out_7, check3_20_out_8, check3_20_out_9,
       not_2_out;

  not not_1 (out_11, 1'b1);
  check3 check3_1 (
    .in_1(not_2_out), .in_2(not_2_out), .in_3(not_2_out), .in_4(check3_8_out_6), .out_7(check3_1_out_7),
    .out_8(check3_1_out_8), .out_9(check3_1_out_9));  // open: out_5, out_6
  check3 check3_2 (
    .in_1(check3_1_out_7), .in_2(check3_1_out_8), .in_3(check3_1_out_9), .in_4(check3_9_out_6),
    .out_7(check3_2_out_7), .out_8(check3_2_out_8), .out_9(check3_2_out_9));  // open: out_5, out_6
  check3 check3_3 (
    .in_1(check3_2_out_7), .in_2(check3_2_out_8), .in_3(check3_2_out_9), .in_4(check3_10_out_6),
    .out_7(check3_3_out_7), .out_8(check3_3_out_8), .out_9(check3_3_out_9));  // open: out_5, out_6
  check3 check3_4 (
    .in_1(check3_3_out_7), .in_2(check3_3_out_8), .in_3(check3_3_out_9), .in_4(check3_11_out_6),
    .out_6(out_14), .out_7(out_15), .out_8(out_16), .out_9(out_17));  // open: out_5
  not not_2 (not_2_out, 1'b1);
  check3 check3_5 (
    .in_1(not_2_out), .in_2(not_2_out), .in_3(not_2_out), .in_4(check3_13_out_6), .out_7(check3_5_out_7),
    .out_8(check3_5_out_8), .out_9(check3_5_out_9));  // open: out_5, out_6
  check3 check3_6 (
    .in_1(check3_5_out_7), .in_2(check3_5_out_8), .in_3(check3_5_out_9), .in_4(check3_14_out_6),
    .out_7(check3_6_out_7), .out_8(check3_6_out_8), .out_9(check3_6_out_9));  // open: out_5, out_6
  check3 check3_7 (
    .in_1(check3_6_out_7), .in_2(check3_6_out_8), .in_3(check3_6_out_9), .in_4(check3_15_out_6),
    .out_7(check3_7_out_7), .out_8(check3_7_out_8), .out_9(check3_7_out_9));  // open: out_5, out_6
  check3 check3_8 (
    .in_1(check3_7_out_7), .in_2(check3_7_out_8), .in_3(check3_7_out_9), .in_4(check3_16_out_6),
    .out_6(check3_8_out_6), .out_7(check3_8_out_7), .out_8(check3_8_out_8), .out_9(check3_8_out_9));  // open: out_5
  check3 check3_9 (
    .in_1(check3_8_out_7), .in_2(check3_8_out_8), .in_3(check3_8_out_9), .in_4(check3_17_out_6),
    .out_6(check3_9_out_6), .out_7(check3_9_out_7), .out_8(check3_9_out_8), .out_9(check3_9_out_9));  // open: out_5
  check3 check3_10 (
    .in_1(check3_9_out_7), .in_2(check3_9_out_8), .in_3(check3_9_out_9), .in_4(check3_18_out_6),
    .out_6(check3_10_out_6), .out_7(check3_10_out_7), .out_8(check3_10_out_8), .out_9(check3_10_out_9));  // open: out_5
  check3 check3_11 (
    .in_1(check3_10_out_7), .in_2(check3_10_out_8), .in_3(check3_10_out_9), .in_4(check3_19_out_6),
    .out_6(check3_11_out_6), .out_7(check3_11_out_7), .out_8(check3_11_out_8), .out_9(check3_11_out_9));  // open: out_5
  check3 check3_12 (
    .in_1(check3_11_out_7), .in_2(check3_11_out_8), .in_3(check3_11_out_9), .in_4(check3_20_out_6),
    .out_6(out_18), .out_7(out_19), .out_8(out_20), .out_9(out_21));  // open: out_5
  check3 check3_13 (
    .in_1(not_2_out), .in_2(not_2_out), .in_3(not_2_out), .in_4(in_1), .out_6(check3_13_out_6),
    .out_7(check3_13_out_7), .out_8(check3_13_out_8), .out_9(check3_13_out_9));  // open: out_5
  check3 check3_14 (
    .in_1(check3_13_out_7), .in_2(check3_13_out_8), .in_3(check3_13_out_9), .in_4(in_2),
    .out_6(check3_14_out_6), .out_7(check3_14_out_7), .out_8(check3_14_out_8), .out_9(check3_14_out_9));  // open: out_5
  check3 check3_15 (
    .in_1(check3_14_out_7), .in_2(check3_14_out_8), .in_3(check3_14_out_9), .in_4(in_3),
    .out_6(check3_15_out_6), .out_7(check3_15_out_7), .out_8(check3_15_out_8), .out_9(check3_15_out_9));  // open: out_5
  check3 check3_16 (
    .in_1(check3_15_out_7), .in_2(check3_15_out_8), .in_3(check3_15_out_9), .in_4(in_4),
    .out_6(check3_16_out_6), .out_7(check3_16_out_7), .out_8(check3_16_out_8), .out_9(check3_16_out_9));  // open: out_5
  check3 check3_17 (
    .in_1(check3_16_out_7), .in_2(check3_16_out_8), .in_3(check3_16_out_9), .in_4(in_5),
    .out_6(check3_17_out_6), .out_7(check3_17_out_7), .out_8(check3_17_out_8), .out_9(check3_17_out_9));  // open: out_5
  check3 check3_18 (
    .in_1(check3_17_out_7), .in_2(check3_17_out_8), .in_3(check3_17_out_9), .in_4(in_6),
    .out_6(check3_18_out_6), .out_7(check3_18_out_7), .out_8(check3_18_out_8), .out_9(check3_18_out_9));  // open: out_5
  check3 check3_19 (
    .in_1(check3_18_out_7), .in_2(check3_18_out_8), .in_3(check3_18_out_9), .in_4(in_7),
    .out_6(check3_19_out_6), .out_7(check3_19_out_7), .out_8(check3_19_out_8), .out_9(check3_19_out_9));  // open: out_5
  check3 check3_20 (
    .in_1(check3_19_out_7), .in_2(check3_19_out_8), .in_3(check3_19_out_9), .in_4(in_8),
    .out_6(check3_20_out_6), .out_7(check3_20_out_7), .out_8(check3_20_out_8), .out_9(check3_20_out_9));  // open: out_5
  check3 check3_21 (
    .in_1(check3_20_out_7), .in_2(check3_20_out_8), .in_3(check3_20_out_9), .in_4(in_9), .out_6(out_22),
    .out_7(out_23), .out_8(out_24), .out_9(out_25));  // open: out_5

  assign out_12 = out_11;
  assign out_13 = out_11;
  assign out_26 = in_10;
endmodule
